# Fritzing sketch ESP-LED-CTRL (saved by Fritzing 0.9.3b)
circuit board: 7.3cm x 4cm
breadboards: 1

parts:
  WeMos_D1_Mini1 = WeMos D1 Mini
  J1 = Screw terminal - 2 pins [package=THT]
  J2 = Screw terminal - 2 pins [package=THT]
  J3 = JST-VHR-3N [part_number=JST-VHR-3N package=THT]
  D1 = Schottky Diode [part_number=1N5817 package="300 mil [THT]"]
  U1 = Mini-USB _B_ connector with 5th pin broken out. [package=usb-minib]
  X1 = USB Connectors [package=usb-microb]
  JP1 = Header 5x2 [package=2x5-ra]
  JP3 = Header 4 [package=molex-1x4_lock]
  J4 = Dagu DGServo 9g header (male) [package=THT]
  S1 = Momentary Switch [package=tactile-pth]

nets:
  N1: WeMos_D1_Mini1.3V3, JP3.4
  N2: WeMos_D1_Mini1.5V, D1.cathode
  N3: WeMos_D1_Mini1.A0, JP3.2
  N4: WeMos_D1_Mini1.D1, JP1.3
  N5: WeMos_D1_Mini1.D2, JP1.1
  N6: WeMos_D1_Mini1.D3, JP1.9, S1.3
  N7: WeMos_D1_Mini1.D4, J3.pin2, J3.pin_5
  GND: WeMos_D1_Mini1.G, J1.pin1, J2.pin1, J3.pin3, J3.pin_6, U1.MTN2, U1.MTN4, U1.GND, X1.GND, JP1.2, JP1.4, JP1.6, JP1.8, JP1.10, JP3.1, S1.2
  N8: WeMos_D1_Mini1.RST, JP3.3
  N9: WeMos_D1_Mini1.RX, JP1.5
  N10: WeMos_D1_Mini1.TX, JP1.7
  N11: J1.pin2, J2.pin2, D1.anode
  N12: J3.pin1, J3.pin_4, U1.VBUS, X1.VBUS, J4.gnd
  N13: X1.D+, J4.pulse
  N14: X1.D-, J4.Vcc
